# Fritzing sketch Buggy (saved by Fritzing 1.0.2b)
breadboards: 1

parts:
  A1 = HuskyLens-Vision-Sensor_1  # not connected
  M1 = MH Sensor Series 4-pin IR Sensor/Line follower [package=THT]
  M2 = MH Sensor Series 4-pin IR Sensor/Line follower [package=THT]
  HC-SR04_Sensor_1 = HC-SR04 Ultrasonic Distance Sensor  # not connected
  M3 = gear-motor-encoder-magnet  # not connected
  M4 = gear-motor-encoder-magnet  # not connected
  S1 = Hall Sensor [part_number=WSH130 package=TO92]  # not connected
  S2 = Hall Sensor [part_number=WSH130 package=TO92]  # not connected
  BAT1 = 6xAA battery  # not connected
  A2 = Arduino UNO R4 WiFi
  LED1 = LED - 5mm [color="Red (633nm)" current=0.030A package="5 mm [THT]"]
  S3 = SPST Slide Switch [package="SIP THT"]
  S4 = SPST Slide Switch [package="SIP THT"]
  IC1 = L293D [package=THT]  # not connected

nets:
  N1: M1.pin2, S3.L1
  N2: M1.pin3, M2.pin3, LED1.cathode
  N3: M1.pin4, M2.pin4, S4.COM
  N4: M2.pin2, S3.L2
  N5: A2.Pin_8, S4.L1
  N6: LED1.anode, S3.COM

custom parts:
  HuskyLens-Vision-Sensor_1: Huskylens is an easy-to-use AI Camera | Vision Sensor. DFrobot Huskylens is equipped with multiple functions, such as face recognition, object tracking, object recognition, line tracking, color recognition, and tag(QR code) recognition.
  MH Sensor Series 4-pin IR Sensor/Line follower: modified version of FC-51 from Peter Van Epp (vanepp in forums) This is the 4-pin version of IR line follower module, using the TCRT5000 sensor and LM393 comparator This one has the analogue output pin, in addition to the Digital pin which is set by the trimmer. The Analog pin can feed an Arduino ADC input, for much better level sensing options and less drift than the crappy potentiometer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
  gear-motor-encoder-magnet: Generic gear motor, 3V to 6V, dual output shafts, 1:48 gear ratio with magnet for wheel encoder
  Hall Sensor: A Hall Sensor
  Arduino UNO R4 WiFi: The Arduino UNO R4 WiFi merges the RA4M1 microprocessor from Renesas with the ESP32-S3 from Espressif, creating an all-in-one tool for makers with enhanced processing power and a diverse array of new peripherals.
  SPST Slide Switch: SPST slide switch with inline 100mil spacing through hole connection terminals
